// Logisim project Control Unit.circ as structural Verilog: 2 circuits, main circuit Instruction decoder
module main (
  input  [31:0] Instruction,
  input  [1:0] Flags,
  input  [3:0] R_latencies,
  input  [3:0] W_latencies,
  input  Clock,
  input  KBD_AV,
  output [4:0] Rs,
  output [4:0] Rt,
  output [1:0] Sp_op,
  output [1:0] Pc_op,
  output [15:0] Const,
  output [2:0] Alu_op,
  output out_13,
  output [25:0] Jump,
  output CHIP_S,
  output [1:0] TARGET_ADD,
  output [4:0] Register_write_addres,
  output Const_enable,
  output Const_op,
  output Hi_Lo_enable,
  output Hi_Lo_register_read,
  output Mult_div_enable,
  output [1:0] Mult_div_op,
  output Register_write_enable,
  output DATA_W,
  output R_W_RAM,
  output Immediate_value_enable,
  output out_28,
  output out_29,
  output out_30,
  output out_31,
  output KBD_EN
);

  wire _000000, _111000, _111111, ADD, ADD_out, ADDI, AND, AND_13_out, and_17_out, and_18_out, and_19_out,
       and_20_out, and_21_out, and_22_out, and_23_out, ANDI, BEQ, BGTZ, BLEZ, BLTZ, BNE, comparator_1_lt,
       comparator_2_eq, comparator_3_eq, comparator_4_eq, comparator_7_eq, comparator_11_eq,
       comparator_12_eq, comparator_13_eq, comparator_16_eq, comparator_17_eq, comparator_20_eq,
       comparator_21_eq, comparator_24_eq, comparator_25_eq, comparator_27_eq, comparator_28_eq,
       comparator_30_eq, comparator_32_eq, comparator_33_eq, comparator_35_eq, comparator_38_eq,
       comparator_39_eq, comparator_40_eq, comparator_41_gt, comparator_41_lt, DIV, DIVU, J, JR, LW, MFHI,
       MFLO, MULT, MULU, NOP, NOR, not_1_out, OR, or_1_out, or_2_out, OR_4_out, or_5_out, or_6_out, or_7_out,
       or_8_out, or_9_out, or_11_out, or_12_out, ORI, POP, priority_encoder_1_en_out, priority_encoder_1_out,
       priority_encoder_2_en_out, priority_encoder_3_en_out, priority_encoder_4_en_out,
       priority_encoder_5_en_out, priority_encoder_5_out, priority_encoder_6_en_out, priority_encoder_6_out,
       priority_encoder_7_en_out, priority_encoder_8_en_out, PUSH, SLT, SLT_out, SLTI, SLTIU, SLTU, SLTU_out,
       SUB, SUB_out, SW, XOR, XOR_out, XORI;
  wire [1:0] priority_encoder_2_out, priority_encoder_3_out, priority_encoder_7_out, priority_encoder_8_out;
  wire [2:0] priority_encoder_4_out;
  wire [3:0] BUSY_T, counter_1_q;
  wire [4:0] RD;
  wire [5:0] FUNC, OP;

  Comparator #(.width(4), .mode("unsigned")) comparator_1 (
    .a(R_latencies), .b(W_latencies), .lt(comparator_1_lt));  // open: gt, eq
  Comparator #(.width(6), .mode("unsigned")) comparator_2 (
    .a(6'b100000), .b(FUNC), .eq(comparator_2_eq));  // open: gt, lt
  Comparator #(.width(6), .mode("unsigned")) comparator_3 (
    .a(6'b100100), .b(FUNC), .eq(comparator_3_eq));  // open: gt, lt
  Comparator #(.width(6), .mode("unsigned")) comparator_4 (
    .a(6'b101010), .b(FUNC), .eq(comparator_4_eq));  // open: gt, lt
  Comparator #(.width(6), .mode("unsigned")) comparator_5 (.a(6'b000100), .b(OP), .eq(BEQ));  // open: gt, lt
  Comparator #(.width(6), .mode("unsigned")) comparator_6 (.a(6'b100011), .b(OP), .eq(LW));  // open: gt, lt
  Comparator #(.width(6), .mode("unsigned")) comparator_7 (
    .a(6'b000100), .b(FUNC), .eq(comparator_7_eq));  // open: gt, lt
  Multiplexer #(.width(4), .enable("false")) multiplexer_1 (
    .in0(R_latencies), .in1(W_latencies), .out(BUSY_T), .sel(comparator_1_lt));
  and and_1 (SLT, _000000, comparator_4_eq);
  and and_2 (ADD, _000000, comparator_2_eq);
  and and_3 (AND, _000000, comparator_3_eq);
  and and_4 (out_31, _111111, comparator_7_eq);
  Comparator #(.width(6)) comparator_8 (.a(OP), .b({6{1'b0}}), .eq(_000000));  // open: gt, lt
  Comparator #(.width(6)) comparator_9 (.a(OP), .b(6'b111000), .eq(_111000));  // open: gt, lt
  Comparator #(.width(6)) comparator_10 (.a(OP), .b({6{1'b1}}), .eq(_111111));  // open: gt, lt
  and and_5 (KBD_EN, out_31, KBD_AV);
  Instruction_decoder instruction_decoder_1 (
    .Instruction(Instruction), .FUNC_CODE(FUNC), .OP_CODE(OP), .RS(Rs), .RT(Rt), .RD(RD), .JUMP(Jump),
    .CONST(Const));
  Comparator #(.width(6), .mode("unsigned")) comparator_11 (
    .a(6'b100010), .b(FUNC), .eq(comparator_11_eq));  // open: gt, lt
  Comparator #(.width(6), .mode("unsigned")) comparator_12 (
    .a(6'b100101), .b(FUNC), .eq(comparator_12_eq));  // open: gt, lt
  Comparator #(.width(6), .mode("unsigned")) comparator_13 (
    .a(6'b101011), .b(FUNC), .eq(comparator_13_eq));  // open: gt, lt
  Comparator #(.width(6), .mode("unsigned")) comparator_14 (.a(6'b000101), .b(OP), .eq(BNE));  // open: gt, lt
  Comparator #(.width(6), .mode("unsigned")) comparator_15 (.a(6'b101011), .b(OP), .eq(SW));  // open: gt, lt
  and and_6 (SUB, _000000, comparator_11_eq);
  and and_7 (OR, _000000, comparator_12_eq);
  and and_8 (SLTU, _000000, comparator_13_eq);
  or or_1 (or_1_out, SW, LW);
  or or_2 (or_2_out, POP, PUSH);
  Priority_Encoder #(.select(1)) priority_encoder_1 (
    .in0(SW), .in1(PUSH), .out(priority_encoder_1_out), .en_out(priority_encoder_1_en_out));  // open: gs, en_in
  and and_9 (CHIP_S, ~out_28, not_1_out);  // AND_Gate
  not not_1 (not_1_out, priority_encoder_2_en_out);
  Priority_Encoder #(.select(2)) priority_encoder_2 (
    .in1(or_1_out), .in2(or_2_out), .out(priority_encoder_2_out), .en_out(priority_encoder_2_en_out));  // open: in0, in3, gs, en_in
  Multiplexer #(.enable("false")) multiplexer_2 (
    .in0(priority_encoder_1_out), .in1(1'b0), .out(DATA_W), .sel(priority_encoder_1_en_out));
  Multiplexer #(.width(2), .enable("false")) multiplexer_3 (
    .in0(priority_encoder_2_out), .in1(2'b00), .out(TARGET_ADD), .sel(priority_encoder_2_en_out));
  or or_3 (R_W_RAM, SW, PUSH);
  Comparator #(.width(6), .mode("unsigned")) comparator_16 (
    .a(6'b011000), .b(FUNC), .eq(comparator_16_eq));  // open: gt, lt
  Comparator #(.width(6), .mode("unsigned")) comparator_17 (
    .a(6'b100111), .b(FUNC), .eq(comparator_17_eq));  // open: gt, lt
  Comparator #(.width(6), .mode("unsigned")) comparator_18 (.a(6'b001010), .b(OP), .eq(SLTI));  // open: gt, lt
  Comparator #(.width(6), .mode("unsigned")) comparator_19 (.a(6'b000110), .b(OP), .eq(BLEZ));  // open: gt, lt
  Comparator #(.width(6), .mode("unsigned")) comparator_20 (
    .a({6{1'b0}}), .b(FUNC), .eq(comparator_20_eq));  // open: gt, lt
  and and_10 (MULT, _000000, comparator_16_eq);
  and and_11 (NOR, _000000, comparator_17_eq);
  and and_12 (POP, _111000, comparator_20_eq);
  or u_ADD (ADD_out, ADD, ADDI, MFHI, PUSH, MFLO, LW, SW);
  or u_SUB (SUB_out, SUB, BEQ, BNE);
  or AND_13 (AND_13_out, AND, ANDI);
  or OR_4 (OR_4_out, OR, ORI);
  or u_XOR (XOR_out, XOR, XORI);
  or u_SLT (SLT_out, SLT, SLTI);
  or u_SLTU (SLTU_out, SLTU, SLTIU);
  not not_2 (Mult_div_enable, priority_encoder_3_en_out);
  Priority_Encoder #(.select(2)) priority_encoder_3 (
    .in0(MULT), .in1(MULU), .in2(DIV), .in3(DIVU), .out(priority_encoder_3_out),
    .en_out(priority_encoder_3_en_out));  // open: gs, en_in
  Multiplexer #(.width(2), .enable("false")) multiplexer_4 (
    .in0(priority_encoder_3_out), .in1(2'b00), .out(Mult_div_op), .sel(priority_encoder_3_en_out));
  Comparator #(.width(6), .mode("unsigned")) comparator_21 (
    .a(6'b011001), .b(FUNC), .eq(comparator_21_eq));  // open: gt, lt
  Comparator #(.width(6), .mode("unsigned")) comparator_22 (.a(6'b001011), .b(OP), .eq(SLTIU));  // open: gt, lt
  Comparator #(.width(6), .mode("unsigned")) comparator_23 (.a(6'b000111), .b(OP), .eq(BGTZ));  // open: gt, lt
  Comparator #(.width(6), .mode("unsigned")) comparator_24 (
    .a(6'b101000), .b(FUNC), .eq(comparator_24_eq));  // open: gt, lt
  Comparator #(.width(6), .mode("unsigned")) comparator_25 (
    .a(6'b000001), .b(FUNC), .eq(comparator_25_eq));  // open: gt, lt
  Priority_Encoder priority_encoder_4 (
    .in0(ADD_out), .in1(SUB_out), .in2(AND_13_out), .in3(OR_4_out), .in4(NOR), .in5(XOR_out), .in6(SLT_out),
    .in7(SLTU_out), .out(priority_encoder_4_out), .en_out(priority_encoder_4_en_out));  // open: en_in, gs
  and and_14 (MULU, _000000, comparator_21_eq);
  and and_15 (XOR, _000000, comparator_24_eq);
  and and_16 (PUSH, _111000, comparator_25_eq);
  Multiplexer #(.width(3), .enable("false")) multiplexer_5 (
    .in0(priority_encoder_4_out), .in1(3'b000), .out(Alu_op), .sel(priority_encoder_4_en_out));
  not not_3 (Hi_Lo_enable, priority_encoder_5_en_out);
  Priority_Encoder #(.select(1)) priority_encoder_5 (
    .in0(MFHI), .in1(MFLO), .out(priority_encoder_5_out), .en_out(priority_encoder_5_en_out));  // open: gs, en_in
  Multiplexer #(.enable("false")) multiplexer_6 (
    .in0(priority_encoder_5_out), .in1(1'b0), .out(Hi_Lo_register_read), .sel(priority_encoder_5_en_out));
  or or_5 (or_5_out, Flags[1], Flags[0]);
  and and_17 (and_17_out, ~Flags[1], ~Flags[0]);  // AND_Gate
  and and_18 (and_18_out, Flags[1], ~Flags[0]);  // AND_Gate
  Comparator #(.width(6), .mode("unsigned")) comparator_26 (.a(6'b001100), .b(OP), .eq(ANDI));  // open: gt, lt
  and and_19 (and_19_out, BEQ, Flags[0]);
  and and_20 (and_20_out, ~Flags[0], BNE);  // AND_Gate
  and and_21 (and_21_out, BLEZ, or_5_out);
  Comparator #(.width(6), .mode("unsigned")) comparator_27 (
    .a(6'b011010), .b(FUNC), .eq(comparator_27_eq));  // open: gt, lt
  Comparator #(.width(6), .mode("unsigned")) comparator_28 (
    .a(6'b010000), .b(FUNC), .eq(comparator_28_eq));  // open: gt, lt
  Comparator #(.width(6), .mode("unsigned")) comparator_29 (.a(6'b000001), .b(OP), .eq(BLTZ));  // open: gt, lt
  and and_22 (and_22_out, BGTZ, and_17_out);
  and and_23 (and_23_out, BLTZ, and_18_out);
  or or_6 (or_6_out, ADDI, SLTI, SLTIU, LW, SW);
  or or_7 (or_7_out, ANDI, ORI, XORI);
  and and_24 (DIV, _000000, comparator_27_eq);
  and and_25 (MFHI, _000000, comparator_28_eq);
  Comparator #(.width(6), .mode("unsigned")) comparator_30 (
    .a({6{1'b1}}), .b(FUNC), .eq(comparator_30_eq));  // open: gt, lt
  and and_26 (out_28, _111111, comparator_30_eq);
  or or_8 (or_8_out, and_19_out, and_20_out, and_21_out, and_22_out, and_23_out);
  not not_4 (Const_enable, priority_encoder_6_en_out);
  Multiplexer #(.enable("false")) multiplexer_7 (
    .in0(priority_encoder_6_out), .in1(1'b0), .out(Const_op), .sel(priority_encoder_6_en_out));
  Priority_Encoder #(.select(1)) priority_encoder_6 (
    .in0(or_6_out), .in1(or_7_out), .out(priority_encoder_6_out), .en_out(priority_encoder_6_en_out));  // open: gs, en_in
  Multiplexer #(.width(2), .enable("false")) multiplexer_8 (
    .in0(priority_encoder_7_out), .in1(2'b00), .out(Pc_op), .sel(priority_encoder_7_en_out));
  Priority_Encoder #(.select(2)) priority_encoder_7 (
    .in1(or_8_out), .in2(J), .in3(JR), .out(priority_encoder_7_out), .en_out(priority_encoder_7_en_out));  // open: in0, gs, en_in
  Comparator #(.width(6), .mode("unsigned")) comparator_31 (.a(6'b001101), .b(OP), .eq(ORI));  // open: gt, lt
  Comparator #(.width(6), .mode("unsigned")) comparator_32 (
    .a(6'b011011), .b(FUNC), .eq(comparator_32_eq));  // open: gt, lt
  Comparator #(.width(6), .mode("unsigned")) comparator_33 (
    .a(6'b010010), .b(FUNC), .eq(comparator_33_eq));  // open: gt, lt
  Comparator #(.width(6), .mode("unsigned")) comparator_34 (.a(6'b000010), .b(OP), .eq(J));  // open: gt, lt
  Comparator #(.width(6), .mode("unsigned")) comparator_35 (
    .a(6'b000001), .b(FUNC), .eq(comparator_35_eq));  // open: gt, lt
  and and_27 (DIVU, _000000, comparator_32_eq);
  and and_28 (MFLO, _000000, comparator_33_eq);
  and and_29 (out_29, _111111, comparator_35_eq);
  or or_9 (or_9_out, ADDI, ANDI, ORI, XORI, SLTI, SLTIU, LW);
  Multiplexer #(.width(5), .enable("false")) multiplexer_9 (
    .in0(RD), .in1(Rt), .out(Register_write_addres), .sel(or_9_out));
  Multiplexer #(.width(2), .enable("false")) multiplexer_10 (
    .in0(priority_encoder_8_out), .in1(2'b00), .out(Sp_op), .sel(priority_encoder_8_en_out));
  Priority_Encoder #(.select(2)) priority_encoder_8 (
    .in1(POP), .in2(PUSH), .out(priority_encoder_8_out), .en_out(priority_encoder_8_en_out));  // open: in0, in3, gs, en_in
  Comparator #(.width(6), .mode("unsigned")) comparator_36 (.a(6'b001000), .b(OP), .eq(ADDI));  // open: gt, lt
  Comparator #(.width(6), .mode("unsigned")) comparator_37 (.a(6'b001110), .b(OP), .eq(XORI));  // open: gt, lt
  Comparator #(.width(6), .mode("unsigned")) comparator_38 (
    .a({6{1'b0}}), .b(FUNC), .eq(comparator_38_eq));  // open: gt, lt
  Comparator #(.width(6), .mode("unsigned")) comparator_39 (
    .a(6'b001000), .b(FUNC), .eq(comparator_39_eq));  // open: gt, lt
  or or_10 (Immediate_value_enable, LW, POP);
  and and_30 (JR, _000000, comparator_39_eq);
  Comparator #(.width(6), .mode("unsigned")) comparator_40 (
    .a(6'b000010), .b(FUNC), .eq(comparator_40_eq));  // open: gt, lt
  and and_31 (NOP, _000000, comparator_38_eq);
  and and_32 (out_30, _111111, comparator_40_eq);
  Counter #(.width(4), .max('hf)) counter_1 (
    .count(1'b1), .Q(counter_1_q), .clk(Clock), .clr(comparator_41_lt));  // open: load, D, carry
  Comparator #(.width(4), .mode("unsigned")) comparator_41 (
    .a(BUSY_T), .b(counter_1_q), .gt(comparator_41_gt), .lt(comparator_41_lt));  // open: eq
  or or_11 (or_11_out, out_28, Mult_div_enable, NOP, BEQ, BNE, BLEZ, PUSH, BGTZ, BLTZ, J, JR, SW, out_29);
  or or_12 (or_12_out, out_28, comparator_41_gt);
  not not_5 (Register_write_enable, or_11_out);
  D_Flip_Flop d_ff_1 (.clk(Clock), .D(or_12_out), .Q(out_13));  // open: Qn, preset, en, reset

  // Other names for the same wires on the sheet: ZERO_F = Flags[0]; SIGN_F = Flags[1]; HALT = out_28;
  //   INST[31:0] = Instruction; KBD = out_31; MULT_DIV_OPS = Mult_div_enable; RND = out_30; TTY = out_29

  // Notes on the sheet:
  //   AND
  //   KBD
  //   ADD
  //   SLT
  //   BEQ
  //   LW
  //   OR
  //   SUB
  //   SLTU
  //   BNE
  //   SW
  //   Memory Interface
  //   MULT
  //   NOR
  //   SLTI
  //   BLEZ
  //   POP
  //   Alu Control
  //   Mult/Div unit Control
  //   MULU
  //   XOR
  //   SLTIU
  //   BGTZ
  //   PUSH
  //   DIV
  //   ANDI
  //   MFHI
  //   BLTZ
  //   HALT
  //   Branch Control
  //   Constant unit Control
  //   DIVU
  //   ORI
  //   MFLO
  //   J
  //   TTY
  //   Sp Control
  //   Register Control
  //   NOP
  //   JR
  //   ADDI
  //   XORI
  //   RND
  //   Busy
endmodule

module Instruction_decoder (
  input  [31:0] Instruction,
  output [5:0] OP_CODE,
  output [4:0] RS,
  output [4:0] RT,
  output [4:0] RD,
  output [5:0] FUNC_CODE,
  output [25:0] JUMP,
  output [15:0] CONST
);


  assign CONST = Instruction[15:0];
  assign FUNC_CODE = Instruction[5:0];
  assign JUMP = Instruction[25:0];
  assign OP_CODE = Instruction[31:26];
  assign RD = Instruction[15:11];
  assign RS = Instruction[25:21];
  assign RT = Instruction[20:16];

  // Other names for the same wires on the sheet: INST[31:0] = Instruction
endmodule
