// Logisim project Datapath.circ as structural Verilog: 9 circuits, main circuit main
module main (
  input  [4:0] Register_read_address_1,
  input  [4:0] Register_read_address_2,
  input  [25:0] Jump,
  input  [15:0] Const,
  input  Const_enable,
  input  [2:0] Register_value_select,
  input  [4:0] Register_write_address,
  input  Register_file_write_enable,
  input  Hi_Lo_Register_write,
  input  [1:0] Ram_address_select,
  input  Ram_value_select,
  input  [3:0] Alu_operation_code,
  input  Constant_unit_operation,
  input  [1:0] Branch_op,
  input  Sp_operation_code,
  input  Load_Pc,
  input  Load_Sp,
  input  [31:0] Ram_value,
  input  KBD_AV,
  input  [6:0] KBD_D,
  input  Reset,
  input  Clock,
  output [31:0] Ram_address,
  output [31:0] Ram_value_2,
  output [6:0] TTY,
  output [1:0] Flags
);

  wire [27:0] PC_VALUE;
  wire [29:0] bit_extender_1_out;
  wire [30:0] ALU_RESULT;
  wire [31:0] alu_1_hi, alu_1_lo, bit_extender_2_out, BRANCH_TARGET, constant_unit_1_const_ext, HI, KBD, LO,
       multiplexer_2_out, multiplexer_3_out, multiplexer_4_out, multiplexer_5_out, PC_PLUS_4, RANDOM, RRD2,
       SP, SP_MINUS_4, SP_PLUS_4, SP_VALUE;
  wire [31:7] RRD1;
  wire [31:28] JUMP_V;

  assign bit_extender_1_out = {{14{Const[15]}}, Const};  // Bit_Extender bit_extender_1
  Random #(.width(32)) random_1 (.clk(Clock), .out(RANDOM));  // open: next, clr
  assign bit_extender_2_out = {{25{1'b0}}, KBD_D};  // Bit_Extender bit_extender_2
  Adder #(.width(32)) adder_1 (.a(SP_VALUE), .b(32'h4), .out(SP_PLUS_4));  // open: cin, cout
  Subtractor #(.width(32)) subtractor_1 (.a(SP_VALUE), .b(32'h4), .out(SP_MINUS_4));  // open: bin, bout
  Adder #(.width(32)) adder_2 (.a({JUMP_V, PC_VALUE}), .b(32'h4), .out(PC_PLUS_4));  // open: cin, cout
  constant_unit constant_unit_1 (.in_1(Const), .in_2(Constant_unit_operation), .Const_ext(constant_unit_1_const_ext));
  Multiplexer #(.width(32), .enable("false")) multiplexer_1 (
    .in0({32{1'b1}}), .in1(bit_extender_2_out), .out(KBD), .sel(KBD_AV));
  Adder #(.width(32)) adder_3 (.a(PC_PLUS_4), .b({bit_extender_1_out, 2'b00}), .out(BRANCH_TARGET));  // open: cin, cout
  Multiplexer #(.width(32), .enable("false")) multiplexer_2 (
    .in0(RRD2), .in1(constant_unit_1_const_ext), .out(multiplexer_2_out), .sel(Const_enable));
  Multiplexer #(.select(3), .width(32), .enable("false")) multiplexer_3 (
    .in0({Flags[1], ALU_RESULT}), .in1(Ram_value), .in2(HI), .in3(LO), .in4(RANDOM), .in5(KBD),
    .out(multiplexer_3_out), .sel(Register_value_select));  // open: in6, in7
  Multiplexer #(.width(32), .enable("false")) multiplexer_4 (
    .in0(SP_PLUS_4), .in1(SP_MINUS_4), .out(multiplexer_4_out), .sel(Sp_operation_code));
  alu alu_1 (
    .Number_a({RRD1, TTY}), .Number_b(multiplexer_2_out), .Operation_code(Alu_operation_code),
    .Result({Flags[1], ALU_RESULT}), .LO(alu_1_lo), .HI(alu_1_hi));
  Multiplexer #(.select(2), .width(32), .enable("false")) multiplexer_5 (
    .in0(PC_PLUS_4), .in1(BRANCH_TARGET), .in2({JUMP_V, Jump, 2'b00}), .in3({RRD1, TTY}),
    .out(multiplexer_5_out), .sel(Branch_op));
  Comparator #(.width(32)) comparator_1 (.a({Flags[1], ALU_RESULT}), .b({32{1'b0}}), .eq(Flags[0]));  // open: gt, lt
  hi_lo_register hi_lo_register_1 (
    .number_hight(alu_1_hi), .low_number(alu_1_lo), .Register_write_enable(Hi_Lo_Register_write),
    .clock(Clock), .hight_result(HI), .Low_result(LO), .Reset(Reset));
  register_file register_file_1 (
    .Register_read_address_1(Register_read_address_1), .Register_read_address_2(Register_read_address_2),
    .Register_write_address(Register_write_address), .Data_write(multiplexer_3_out),
    .Register_write_enable(Register_file_write_enable), .Reset(Reset), .Clock(Clock),
    .Register_read_data_1({RRD1, TTY}), .Register_read_data_2(RRD2), .SP_write(Load_Sp),
    .Sp_value(multiplexer_4_out), .Sp_value_2(SP));
  Register #(.width(32)) PC (.D(multiplexer_5_out), .en(Load_Pc), .Q({JUMP_V, PC_VALUE}), .clk(Clock), .clr(Reset));
  Multiplexer #(.select(2), .width(32), .enable("false")) multiplexer_6 (
    .in0({JUMP_V, PC_VALUE}), .in1({Flags[1], ALU_RESULT}), .in2(SP), .out(Ram_address),
    .sel(Ram_address_select));  // open: in3
  Multiplexer #(.width(32), .enable("false")) multiplexer_7 (
    .in0(RRD2), .in1({RRD1, TTY}), .out(Ram_value_2), .sel(Ram_value_select));

  // Other names for the same wires on the sheet: ALU_OP[3:0] = Alu_operation_code; CONST_ENAB = Const_enable;
  //   CONST_OP = Constant_unit_operation; ZERO_F = Flags[0]; ALU_RESULT[31] = Flags[1]; SIGN_F = Flags[1];
  //   HI_LO_W_ENAB = Hi_Lo_Register_write; JUMP_V[27:2] = Jump; PC_VALUE[31:28] = JUMP_V;
  //   RAM_ADDRESS_S[1:0] = Ram_address_select; RAM_VALUE_S = Ram_value_select;
  //   REG_SELECT[2:0] = Register_value_select; REG_W_ADDRESS[4:0] = Register_write_address;
  //   REG_W_ENAB = Register_file_write_enable; RRD1[6:0] = TTY; RS[4:0] = Register_read_address_1;
  //   RT[4:0] = Register_read_address_2; SP_OP = Sp_operation_code
endmodule

module register_file (
  input  [4:0] Register_read_address_1,
  input  [4:0] Register_read_address_2,
  input  [4:0] Register_write_address,
  input  [31:0] Data_write,
  input  Register_write_enable,
  input  [31:0] Sp_value,
  input  SP_write,
  input  Reset,
  input  Clock,
  output [31:0] Sp_value_2,
  output [31:0] Register_read_data_1,
  output [31:0] Register_read_data_2
);

  wire or_1_out, W0, W1, W2, W3, W4, W5, W6, W7, W8, W9, W10, W11, W12, W13, W14, W15, W16, W17, W18, W19,
       W20, W21, W22, W23, W24, W25, W26, W27, W28, W29, W30, W31;
  wire [31:0] multiplexer_3_out, R0, R1, R2, R3, R4, R5, R6, R7, R8, R9, R10, R11, R12, R13, R14, R15, R16,
       R17, R18, R19, R20, R21, R22, R23, R24, R25, R26, R27, R28, R29, R30;

  Decoder #(.select(5), .disabled(0)) decoder_1 (
    .out0(W0), .out1(W1), .out2(W2), .out3(W3), .out4(W4), .out5(W5), .out6(W6), .out7(W7), .out8(W8),
    .out9(W9), .out10(W10), .out11(W11), .out12(W12), .out13(W13), .out14(W14), .out15(W15), .out16(W16),
    .out17(W17), .out18(W18), .out19(W19), .out20(W20), .out21(W21), .out22(W22), .out23(W23), .out24(W24),
    .out25(W25), .out26(W26), .out27(W27), .out28(W28), .out29(W29), .out30(W30), .out31(W31),
    .sel(Register_write_address), .en(Register_write_enable));
  Register #(.width(32)) u_R0 (.D({32{1'b0}}), .en(W0), .Q(R0), .clk(Clock), .clr(Reset));
  Register #(.width(32)) u_R8 (.D(Data_write), .en(W8), .Q(R8), .clk(Clock), .clr(Reset));
  Register #(.width(32)) u_R16 (.D(Data_write), .en(W16), .Q(R16), .clk(Clock), .clr(Reset));
  Register #(.width(32)) u_R24 (.D(Data_write), .en(W24), .Q(R24), .clk(Clock), .clr(Reset));
  Register #(.width(32)) u_R1 (.D(Data_write), .en(W1), .Q(R1), .clk(Clock), .clr(Reset));
  Register #(.width(32)) u_R9 (.D(Data_write), .en(W9), .Q(R9), .clk(Clock), .clr(Reset));
  Register #(.width(32)) u_R17 (.D(Data_write), .en(W17), .Q(R17), .clk(Clock), .clr(Reset));
  Register #(.width(32)) u_R25 (.D(Data_write), .en(W25), .Q(R25), .clk(Clock), .clr(Reset));
  Register #(.width(32)) u_R2 (.D(Data_write), .en(W2), .Q(R2), .clk(Clock), .clr(Reset));
  Register #(.width(32)) u_R10 (.D(Data_write), .en(W10), .Q(R10), .clk(Clock), .clr(Reset));
  Register #(.width(32)) u_R18 (.D(Data_write), .en(W18), .Q(R18), .clk(Clock), .clr(Reset));
  Register #(.width(32)) u_R26 (.D(Data_write), .en(W26), .Q(R26), .clk(Clock), .clr(Reset));
  Multiplexer #(.select(5), .width(32), .enable("false")) multiplexer_1 (
    .in0(R0), .in1(R1), .in2(R2), .in3(R3), .in4(R4), .in5(R5), .in6(R6), .in7(R7), .in8(R8), .in9(R9),
    .in10(R10), .in11(R11), .in12(R12), .in13(R13), .in14(R14), .in15(R15), .in16(R16), .in17(R17),
    .in18(R18), .in19(R19), .in20(R20), .in21(R21), .in22(R22), .in23(R23), .in24(R24), .in25(R25),
    .in26(R26), .in27(R27), .in28(R28), .in29(R29), .in30(R30), .in31(Sp_value_2),
    .out(Register_read_data_1), .sel(Register_read_address_1));
  Register #(.width(32)) u_R3 (.D(Data_write), .en(W3), .Q(R3), .clk(Clock), .clr(Reset));
  Register #(.width(32)) u_R11 (.D(Data_write), .en(W11), .Q(R11), .clk(Clock), .clr(Reset));
  Register #(.width(32)) u_R19 (.D(Data_write), .en(W19), .Q(R19), .clk(Clock), .clr(Reset));
  Register #(.width(32)) u_R27 (.D(Data_write), .en(W27), .Q(R27), .clk(Clock), .clr(Reset));
  Register #(.width(32)) u_R4 (.D(Data_write), .en(W4), .Q(R4), .clk(Clock), .clr(Reset));
  Register #(.width(32)) u_R12 (.D(Data_write), .en(W12), .Q(R12), .clk(Clock), .clr(Reset));
  Register #(.width(32)) u_R20 (.D(Data_write), .en(W20), .Q(R20), .clk(Clock), .clr(Reset));
  Register #(.width(32)) u_R28 (.D(Data_write), .en(W28), .Q(R28), .clk(Clock), .clr(Reset));
  Register #(.width(32)) u_R5 (.D(Data_write), .en(W5), .Q(R5), .clk(Clock), .clr(Reset));
  Register #(.width(32)) u_R13 (.D(Data_write), .en(W13), .Q(R13), .clk(Clock), .clr(Reset));
  Register #(.width(32)) u_R21 (.D(Data_write), .en(W21), .Q(R21), .clk(Clock), .clr(Reset));
  Register #(.width(32)) u_R29 (.D(Data_write), .en(W29), .Q(R29), .clk(Clock), .clr(Reset));
  Multiplexer #(.select(5), .width(32), .enable("false")) multiplexer_2 (
    .in0(R0), .in1(R1), .in2(R2), .in3(R3), .in4(R4), .in5(R5), .in6(R6), .in7(R7), .in8(R8), .in9(R9),
    .in10(R10), .in11(R11), .in12(R12), .in13(R13), .in14(R14), .in15(R15), .in16(R16), .in17(R17),
    .in18(R18), .in19(R19), .in20(R20), .in21(R21), .in22(R22), .in23(R23), .in24(R24), .in25(R25),
    .in26(R26), .in27(R27), .in28(R28), .in29(R29), .in30(R30), .in31(Sp_value_2),
    .out(Register_read_data_2), .sel(Register_read_address_2));
  Register #(.width(32)) u_R6 (.D(Data_write), .en(W6), .Q(R6), .clk(Clock), .clr(Reset));
  Register #(.width(32)) u_R14 (.D(Data_write), .en(W14), .Q(R14), .clk(Clock), .clr(Reset));
  Register #(.width(32)) u_R22 (.D(Data_write), .en(W22), .Q(R6), .clk(Clock), .clr(Reset));
  Register #(.width(32)) u_R30 (.D(Data_write), .en(W30), .Q(R30), .clk(Clock), .clr(Reset));
  Register #(.width(32)) u_R7 (.D(Data_write), .en(W7), .Q(R7), .clk(Clock), .clr(Reset));
  Register #(.width(32)) u_R15 (.D(Data_write), .en(W15), .Q(R15), .clk(Clock), .clr(Reset));
  Register #(.width(32)) u_R23 (.D(Data_write), .en(W23), .Q(R23), .clk(Clock), .clr(Reset));
  Multiplexer #(.width(32), .enable("false")) multiplexer_3 (
    .in0(Data_write), .in1(Sp_value), .out(multiplexer_3_out), .sel(SP_write));
  or or_1 (or_1_out, SP_write, W31);
  Register #(.width(32)) SP (.D(multiplexer_3_out), .en(or_1_out), .Q(Sp_value_2), .clk(Clock), .clr(Reset));

  // Other names for the same wires on the sheet: R31[31:0] = Sp_value_2; RR1[4:0] = Register_read_address_1;
  //   RR2[4:0] = Register_read_address_2; RW[4:0] = Register_write_address; RWE = Register_write_enable;
  //   SP_W = SP_write; W_DATA[31:0] = Data_write
endmodule

module alu (
  input  [31:0] Number_a,
  input  [31:0] Number_b,
  input  [3:0] Operation_code,
  output [31:0] HI,
  output [31:0] LO,
  output [31:0] Result
);

  wire [0:0] SLT, SLTU;
  wire [31:0] ADD, AND, DIV_HI, DIV_LO, DIVU_HI, DIVU_LO, MULT_HI, MULT_LO, MULU_HI, MULU_LO, not_1_out, OR,
       SUB, XOR;

  Adder #(.width(32)) adder_1 (.a(Number_a), .b(Number_b), .out(ADD));  // open: cin, cout
  Subtractor #(.width(32)) subtractor_1 (.a(Number_a), .b(Number_b), .out(SUB));  // open: bin, bout
  assign AND = Number_a & Number_b;  // AND_Gate and_1, 32 bits wide
  mult_op mult_op_1 (.Number_a(Number_a), .Number_b(Number_b), .Low_result(MULT_LO), .Hight_result(MULT_HI));
  assign not_1_out = ~OR;  // NOT_Gate not_1, 32 bits wide
  assign OR = Number_a | Number_b;  // OR_Gate or_1, 32 bits wide
  Multiplexer #(.select(4), .width(32), .enable("false")) multiplexer_1 (
    .in0(ADD), .in1(SUB), .in2(AND), .in3(OR), .in4(not_1_out), .in5(XOR), .in6({{31{1'b0}}, SLT[0]}),
    .in7({{31{1'b0}}, SLTU[0]}), .out(Result), .sel(Operation_code));  // open: in8, in9, in10, in11, in12, in13, in14, in15
  Multiplier #(.width(32)) multiplier_1 (.a(Number_a), .b(Number_b), .out(MULU_LO), .cout(MULU_HI));  // open: cin
  assign XOR = Number_a ^ Number_b;  // XOR_Gate xor_1, 32 bits wide
  Comparator #(.width(32)) comparator_1 (.a(Number_a), .b(Number_b), .lt(SLT[0]));  // open: gt, eq
  div_op div_op_1 (.Number_a(Number_a), .Number_b(Number_b), .Low(DIV_LO), .Hight(DIV_HI));
  Multiplexer #(.select(4), .width(32), .enable("false")) multiplexer_2 (
    .in8(MULT_HI), .in9(MULU_HI), .in10(DIV_HI), .in11(DIVU_HI), .out(HI), .sel(Operation_code));  // open: in0, in1, in2, in3, in4, in5, in6, in7, in12, in13, in14, in15
  Comparator #(.width(32), .mode("unsigned")) comparator_2 (.a(Number_a), .b(Number_b), .lt(SLTU[0]));  // open: gt, eq
  Divider #(.width(32)) divider_1 (.a(Number_a), .b(Number_b), .out(DIVU_LO), .rem(DIVU_HI));  // open: upper
  Multiplexer #(.select(4), .width(32), .enable("false")) multiplexer_3 (
    .in8(MULT_LO), .in9(MULU_LO), .in10(DIV_LO), .in11(DIVU_LO), .out(LO), .sel(Operation_code));  // open: in0, in1, in2, in3, in4, in5, in6, in7, in12, in13, in14, in15

  // Other names for the same wires on the sheet: OP[3:0] = Operation_code; RS[31:0] = Number_a; RT[31:0] = Number_b

  // Notes on the sheet:
  //   ADD
  //   SUB
  //   AND
  //   MULT
  //   OR
  //   MULU
  //   XOR
  //   DIV
  //   SLT
  //   SLTU
  //   DIVU
endmodule

module mult_op (
  input  [31:0] Number_a,
  input  [31:0] Number_b,
  output [31:0] Low_result,
  output [31:0] Hight_result
);

  wire adder_1_cout, SIGN;
  wire [31:0] absolute_value_1_absolute_value, absolute_value_2_absolute_value, adder_1_out, adder_2_out,
       bit_extender_1_out, multiplier_1_cout, multiplier_1_out, not_1_out, not_2_out;

  xor xor_1 (SIGN, Number_a[31], Number_b[31]);
  absolute_value absolute_value_1 (.Number(Number_a), .Absolute_value(absolute_value_1_absolute_value));
  absolute_value absolute_value_2 (.Number(Number_b), .Absolute_value(absolute_value_2_absolute_value));
  Multiplier #(.width(32)) multiplier_1 (
    .a(absolute_value_1_absolute_value), .b(absolute_value_2_absolute_value), .out(multiplier_1_out),
    .cout(multiplier_1_cout));  // open: cin
  assign not_1_out = ~multiplier_1_out;  // NOT_Gate not_1, 32 bits wide
  assign not_2_out = ~multiplier_1_cout;  // NOT_Gate not_2, 32 bits wide
  Adder #(.width(32)) adder_1 (.a(not_1_out), .b(32'h1), .out(adder_1_out), .cout(adder_1_cout));  // open: cin
  assign bit_extender_1_out = {{31{1'b0}}, adder_1_cout};  // Bit_Extender bit_extender_1
  Adder #(.width(32)) adder_2 (.a(bit_extender_1_out), .b(not_2_out), .out(adder_2_out));  // open: cin, cout
  Multiplexer #(.width(32), .enable("false")) multiplexer_1 (
    .in0(multiplier_1_cout), .in1(adder_2_out), .out(Hight_result), .sel(SIGN));
  Multiplexer #(.width(32), .enable("false")) multiplexer_2 (
    .in0(multiplier_1_out), .in1(adder_1_out), .out(Low_result), .sel(SIGN));

  // Other names for the same wires on the sheet: RS[31:0] = Number_a; RT[31:0] = Number_b
endmodule

module absolute_value (
  input  [31:0] Number,
  output [31:0] Absolute_value
);

  wire [31:0] two_s_complement_1_complement;

  two_s_complement two_s_complement_1 (.Number(Number), .Complement(two_s_complement_1_complement));
  Multiplexer #(.width(32), .enable("false")) multiplexer_1 (
    .in0(Number), .in1(two_s_complement_1_complement), .out(Absolute_value), .sel(Number[31]));
endmodule

module two_s_complement (
  input  [31:0] Number,
  output [31:0] Complement
);

  wire [31:0] not_1_out;

  assign not_1_out = ~Number;  // NOT_Gate not_1, 32 bits wide
  Adder #(.width(32)) adder_1 (.a(not_1_out), .b(32'h1), .out(Complement));  // open: cin, cout
endmodule

module div_op (
  input  [31:0] Number_a,
  input  [31:0] Number_b,
  output [31:0] Low,
  output [31:0] Hight
);

  wire SIGN;
  wire [31:0] absolute_value_1_absolute_value, absolute_value_2_absolute_value, divider_1_out, divider_1_rem,
       two_s_complement_1_complement, two_s_complement_2_complement;

  xor xor_1 (SIGN, Number_a[31], Number_b[31]);
  absolute_value absolute_value_1 (.Number(Number_a), .Absolute_value(absolute_value_1_absolute_value));
  absolute_value absolute_value_2 (.Number(Number_b), .Absolute_value(absolute_value_2_absolute_value));
  Divider #(.width(32)) divider_1 (
    .a(absolute_value_1_absolute_value), .b(absolute_value_2_absolute_value), .out(divider_1_out),
    .rem(divider_1_rem));  // open: upper
  two_s_complement two_s_complement_1 (.Number(divider_1_out), .Complement(two_s_complement_1_complement));
  two_s_complement two_s_complement_2 (.Number(divider_1_rem), .Complement(two_s_complement_2_complement));
  Multiplexer #(.width(32), .enable("false")) multiplexer_1 (
    .in0(divider_1_out), .in1(two_s_complement_1_complement), .out(Low), .sel(SIGN));
  Multiplexer #(.width(32), .enable("false")) multiplexer_2 (
    .in0(divider_1_rem), .in1(two_s_complement_2_complement), .out(Hight), .sel(Number_a[31]));

  // Other names for the same wires on the sheet: RS[31:0] = Number_a; RT[31:0] = Number_b
endmodule

module hi_lo_register (
  input  [31:0] number_hight,
  input  [31:0] low_number,
  input  Register_write_enable,
  input  Reset,
  input  clock,
  output [31:0] hight_result,
  output [31:0] Low_result
);

  wire W;

  Register #(.width(32)) HI (.D(number_hight), .en(W), .Q(hight_result), .clk(clock), .clr(Reset));
  Register #(.width(32)) LO (.D(low_number), .en(W), .Q(Low_result), .clk(clock), .clr(Reset));

  // Other names for the same wires on the sheet: W_HI[31:0] = number_hight; W_LO[31:0] = low_number;
  //   Write = Register_write_enable
endmodule

module constant_unit (
  input  [15:0] in_1,
  input  in_2,
  output [31:0] Const_ext
);

  wire [31:0] bit_extender_1_out, bit_extender_2_out;

  assign bit_extender_1_out = {{16{in_1[15]}}, in_1};  // Bit_Extender bit_extender_1
  assign bit_extender_2_out = {{16{1'b0}}, in_1};  // Bit_Extender bit_extender_2
  Multiplexer #(.width(32), .enable("false")) multiplexer_1 (
    .in0(bit_extender_1_out), .in1(bit_extender_2_out), .out(Const_ext), .sel(in_2));

  // Other names for the same wires on the sheet: CONST[15:0] = in_1; OP = in_2
endmodule
